# Fritzing sketch meadow-lm35 (saved by Fritzing 0.9.6b)
breadboards: 1

parts:
  Mod1 = Meadow F7 Micro
  T1 = LM35 Temperature Sensor [package="TO92 [THT]"]

nets:
  GND: Mod1.GND, T1.GND
  N1: Mod1.A1, T1.Vout
  N2: Mod1.+5V, T1.+Vs
